# Fritzing sketch circuit for 4 bit serial input  (saved by Fritzing 0.9.2b)
breadboards: 3

parts:
  U1 = 555 Timer [package="DIP8 [THT]"]
  S1 = SWITCH-MOMENTARY-2 [package=tactile-pth]
  S2 = SWITCH-MOMENTARY-2 [package=tactile-pth]
  C1 = Capacitor Polarized [package=cpol-radial-10uf-25v]
  C2 = Capacitor Polarized [package=cpol-radial-10uf-25v]
  R1 = Resistor [tolerance=±5% resistance=1k package="0402 [SMD]"]
  R2 = Resistor [tolerance=±5% resistance=1k package="0402 [SMD]"]
  IC1 = IC, DIP package, 14 pins [chip_label="IC 74132"]
  C3 = Capacitor [package=cap-pth-small2]
  U2 = 555 Timer [package="DIP8 [THT]"]
  C4 = Capacitor [package=cap-pth-small2]
  R4 = Rotary Potentiometer (Small) [maximum_resistance=100kΩ package=THT]
  C5 = Electrolytic Capacitor [capacitance=1µF package="100 mil [THT, electrolytic]"]
  IC8 = IC, DIP package, 14 pins [chip_label="IC 7404(NOT)"]
  IC9 = IC, DIP package, 16 pins [chip_label="IC 74112"]
  IC4 = IC, DIP package, 16 pins [chip_label="IC 74112"]
  LED3 = LED - 5mm [color="Red (633nm)" package="5 mm [THT]"]
  LED4 = LED - 5mm [color="Red (633nm)" package="5 mm [THT]"]
  LED5 = LED - 5mm [color="Red (633nm)" package="5 mm [THT]"]
  LED6 = LED - 5mm [color="Red (633nm)" package="5 mm [THT]"]
  R5 = Resistor [tolerance=±5% resistance=220 package=THT]
  R6 = Resistor [tolerance=±5% resistance=220 package=THT]
  R7 = Resistor [tolerance=±5% resistance=220 package=THT]
  R8 = Resistor [tolerance=±5% resistance=220 package=THT]
  IC11 = IC, DIP package, 14 pins [chip_label=IC7404]
  LED7 = LED - 5mm [color="Orange (612nm)" package="5 mm [THT]"]
  LED1 = smd LED [color="Red (633nm)" package="0805 [SMD]"]
  LED2 = smd LED [color="Red (633nm)" package="0603 [SMD]"]
  LED2_2 = LED - 3mm [color="Red (633nm)" package="3 mm [THT]"]
  IC10 = IC, DIP package, 14 pins [chip_label=IC7408]
  IC2 = IC, DIP package, 14 pins [chip_label=IC7432]

nets:
  N1: U1.Ground, U1.Threshold, S1.1, S2.1, C1.+, C2.+, IC1.pin7, C3.1, U2.Ground, C4.1, C5.-, LED1.cathode, LED2.cathode, LED2_2.cathode, IC2.pin7
  N2: U1.Trigger, IC1.pin4, IC2.pin1
  N3: U1.Output, IC8.pin5, IC9.pin3, LED1.anode
  N4: U1.Reset, IC1.pin10, IC2.pin2
  N5: U1.Control_Voltage, C3.2
  N6: U1.Vcc_Supply_Voltage, R1.Pin_0, R2.Pin_1, IC1.pin14, U2.Vcc_Supply_Voltage, IC2.pin14
  N7: S1.2, C2.-, R1.Pin_1, IC1.pin1
  N8: S2.2, C1.-, R2.Pin_0, IC1.pin13
  N9: IC1.pin2, IC1.pin3
  N10: IC1.pin11, IC1.pin12
  N11: U2.Trigger, IC2.pin3
  N12: U2.Output, IC9.pin1, IC9.pin13, IC4.pin1, IC4.pin13, LED2.anode, LED2_2.anode
  N13: U2.Reset, R4.wiper
  N14: U2.Control_Voltage, C4.2
  N15: U2.Threshold, U2.Discharge, R4.leg1, C5.+
  N16: IC8.pin6, IC9.pin2
  N17: IC8.pin7, IC9.pin8, IC4.pin8, R5.Pin_1, R6.Pin_1, R7.Pin_1, R8.Pin_1, IC11.pin7, LED7.cathode, IC10.pin7
  N18: IC8.pin14, IC9.pin14, IC9.pin15, IC9.pin16, IC4.pin14, IC4.pin15, IC4.pin16, IC11.pin14, IC10.pin14
  N19: IC9.pin4, IC9.pin10, IC4.pin4, IC4.pin10
  N20: IC9.pin5, IC9.pin11, LED4.anode, IC10.pin13
  N21: IC9.pin6, IC9.pin12
  N22: IC9.pin7, IC4.pin2
  N23: IC9.pin9, IC4.pin3, LED3.anode, IC10.pin12
  N24: IC4.pin5, IC4.pin11, LED5.anode, IC11.pin13
  N25: IC4.pin6, IC4.pin12
  N26: IC4.pin9, LED6.anode
  N27: LED3.cathode, R6.Pin_0
  N28: LED4.cathode, R5.Pin_0
  N29: LED5.cathode, R7.Pin_0
  N30: LED6.cathode, R8.Pin_0
  N31: IC11.pin12, IC10.pin5
  N32: LED7.anode, IC10.pin6
  N33: IC10.pin4, IC10.pin8
  N34: IC10.pin10, IC10.pin11
